# Fritzing sketch Dmxuino-01 (saved by Fritzing 0.9.2b)
breadboards: 1

parts:
  U1 = MAX485 [package=dil08]
  XLRout = XLR3_NCFAH2 [package=xlr3_nc3fah2]
  µP = Arduino Uno (Rev3) - ICSP
  C1 = Ceramic Capacitor [capacitance=1µF package="100 mil [THT, multilayer]"]
  part = XLR3_NCFAH2 [package=xlr3_nc3fah2]  # not connected
  R1 = Resistor [tolerance=±5% resistance=100 package=THT]
  R2 = Resistor [tolerance=±5% resistance=120 package=THT]

nets:
  N1: U1.RO, R1.Pin_1
  GND: U1.RE, U1.GND, XLRout.1, XLRout.G, µP.GND, C1.0, R1.Pin_0
  VCC: U1.DE, U1.VCC, µP.5V, C1.1
  N2: U1.DI, µP.D1/TX
  N3: U1.A, XLRout.3, R2.Pin_1
  N4: U1.B, XLRout.2, R2.Pin_0
